// Logisim project PLUV2.circ as structural Verilog: 5 circuits, main circuit main
module main (
);

  wire and_1_out, clock_1_out, d_ff_1_q, d_ff_1_qn, plu_1_pixel_clk;
  wire [1:0] rom_2_data_2;
  wire [3:0] counter_1_q;
  wire [15:0] counter_2_q;
  wire [23:0] plu_1_rgb_output_24, rom_1_data, rom_3_data;
  wire [29:0] rom_2_data;

  D_Flip_Flop d_ff_1 (.D(d_ff_1_qn), .clk(clock_1_out), .Q(d_ff_1_q), .Qn(d_ff_1_qn));  // open: preset, reset
  and and_1 (and_1_out, rom_2_data_2[0], d_ff_1_qn);
  Counter #(.max('hf), .width(4)) counter_1 (
    .clr(and_1_out), .clk(d_ff_1_q), .D(4'b1111), .Q(counter_1_q));  // open: load, up, count, carry
  ROM #(.addrWidth(4), .dataWidth(24)) rom_1 (.addr(counter_1_q), .data(rom_1_data));
  ROM #(.addrWidth(4), .dataWidth(32)) rom_2 (.addr(counter_1_q), .data({rom_2_data_2, rom_2_data}));
  ROM #(.addrWidth(16), .dataWidth(24)) rom_3 (.addr(counter_2_q), .data(rom_3_data));
  Clock clock_1 (.out(clock_1_out));
  // Probe on rom_2_data[29:27]
  // Probe on rom_2_data[26:24]
  // Probe on rom_2_data[23:18]
  // Probe on rom_2_data[17:0]
  // Probe on rom_3_data
  Counter #(.max('hffff), .width(16)) counter_2 (
    .clk(plu_1_pixel_clk), .D({16{1'b1}}), .Q(counter_2_q));  // open: clr, load, up, count, carry
  PLU plu_1 (
    .DATA_A_IN_24(rom_3_data), .DATA_B_IN_24(rom_1_data), .EN_A_3(rom_2_data[29:27]),
    .EN_B_3(rom_2_data[26:24]), .Channel_Swap_6(rom_2_data[23:18]), .CLK(clock_1_out),
    .opcode_in_18(rom_2_data[17:0]), .RGB_OUTPUT_24(plu_1_rgb_output_24), .pixel_clk(plu_1_pixel_clk));
  // Probe on plu_1_rgb_output_24
  // RGB_Video #(.height(256), .scale(4), .width(256)) rgb_video_1: pin names not known; wires that end beside it: plu_1_pixel_clk, 1'b1, counter_2_q[7:0], counter_2_q[15:8], plu_1_rgb_output_24

  // Notes on the sheet:
  //   contents of rom_2 (hex, n*v repeats v):
  //   3f190410 7f1b0c30 13*3f180000 3f1b0c30
  //   contents of rom_3 (hex, n*v repeats v):
  //   13140f 14140f 151510 151510 161610 161610 151510 14150f 141610 161710 171811 181811 181810 171710
  //   171710 171710 171811 161710 14150e 14140e 13110b 130f04 1e2b2f 235980 19425b 10150b 1a1406 251912
  //   2c1812 371812 421711 481811 4b1912 4b1a13 4a1b13 461e13 442312 452a12 483614 514416 5c5015 6a5914
  //   776114 7f6415 826617 7c6416 765f13 705c14 655513 6a4e11 7e4a10 7c491b 61441d 3b2c0e 584315 604b18
  //   6b4b10 a36205 c68008 cf9714 daab27 e2b839 e7c149 ebc655 eeca5c efcb5f f0cb5e f0c95b efc455 f0bd55
  //   f2b960 f7b76f fab27d fbac86 fba387 fb967e f47e64 dc5a41 ce4a36 da5748 ee706b fa8488 fc919a fd95a1
  //   fd95a2 fd8f9c fc818d f66a72 e85056 e44d52 e94c52 c9322f 97180b 931e13 85221a 78211b 7b231e 8c2823
  //   972a25 9e2e29 9c342d 84322a 70392b 674330 bc2f2d fb2d40 fc4f65 fb435b ef546e 949ebd 4f9fc8 7fa6cf
  //   c6bd9c efc94d 95a89e 709bcf ccb64d c7ac25 977f3c 9d6244 c38f9c d0c4ea f38492 cb1816 9d0000 bc1415
  //   d42c2d b9191c a20000 c5241e e47771 d28654 a87427 88743d a48230 e07116 f08484 81a4d1 3d9ebf 469cb7
  //   469bb8 3c98b6 8aabbf c7b9c4 569fbe 3f9ab8 4c9cb8 4d9cb9 479bb9 459ab8 469cbb 499bc7 8c9a9f e2ad35
  //   d9bb59 6aa2c0 2e96ca 5a98b0 ccac75 a8b39f 4c94bf 85899d d7a08f fbb793 f3c3b9 81a8c8 2795b6 3d99b6
  //   449ab7 419ab6 409ab6 3e9ab6 3c99b5 3b99b5 3b99b5 3899b5 3698b4 3698b4 3898b4 3598b4 3398b4 3498b4
  //   3597b4 3497b3 3397b4 3297b3 3197b4 2d96b2 2b96b2 2e96b3 3096b3 2f95b2 2c95b1 2b95b1 2d95b2 2c94b1
  //   2b94b1 2c94b1 2b94b1 2c94b1 2b94b1 2993b0 2993b0 2793b0 2492af 2492af 2492af 2392af 2191ae 2090ad
  //   2090ad 2090ad 208fad 1f90ad 1b8eac 198eac 198eac 1a8eac 1a8dab 1b8dac 1b8dab 198cab 168baa 148baa
  //   138aa9 138aa9 128aa9 1089a7 f88a7 f88a7 e88a7 c87a6 c87a6 d86a5 c86a5 b85a5 b84a4 a84a3 a84a3 883a2
  //   883a2 782a1 781a1 680a0 6809f 6809f 57e9e 57e9d 47d9d 47c9d 47b9c 47b9b 47b9b 37b9b 37a9b 3799a
  //   12140f 14150f 141510 161611 161611 161610 151510 161610 161710 181810 191911 191911 181811 171710
  //   161710 14160f 14160f 12140d 10120c 14150f 13130d 120f07 1a211e 1a4058 123b55 172121 251a0f 2d1a13
  //   311813 391711 441611 4a1712 4c1812 4b1912 491b13 461e12 432212 442a12 473414 504316 5b4f16 675714
  //   745e14 7c6215 816517 7c6216 745e13 6e5b14 665413 735011 854711 6d3e17 4b3414 2a1c02 47330d 5a4617
  //   644913 9c5f08 c67d07 cf9511 d7a925 e1b839 e7c14a ebc756 eecb5d efcb5f f0ca5e f0c95a efc355 f1bf58
  //   f5bc66 f8b973 fbb380 fbac86 fba283 fa9174 ef7558 d9543b d24b37 e15c50 f27471 fa8689 fc929c fd97a4
  //   fd95a3 fd8e9c fb7f8b f4666e e95359 ec5963 f45863 d73839 991b0f 8c1e11 7e2219 6f221b 71241d 7e2721
  //   862822 8c2b24 90322a 783027 5d3225 613f2c b53430 f92336 f9354c f84158 f7667d c2bad0 95bfdc a3aed2
  //   a3afbb b9b680 96a6ad 8e9cc9 dbb74f c9b211 938012 895e16 9d786b a0a5d6 e694ae e82c2b aa0000 b20d0e
  //   c92424 ba1717 a90202 c62b25 e4734a d28425 a87b10 837226 9c831b d98e09 f7a56b 9dafca 439dc3 439ab8
  //   479bb8 3d98b8 81a9bf e2bfbf 77a7bd 3899b9 469ab8 4298b6 4097b8 4298bb 449bbb 449cc6 759aaf daac45
  //   d8b95c 62a0c0 2896c7 5899b7 c6a286 98a3a3 498fb6 9c8c90 e5a285 e0a370 e8b18c 91abbf 2e96bb 3e99b7
  //   449bb7 3f99b5 3f9ab6 3e9ab6 3c9ab6 3b99b5 3c9ab6 3999b5 3699b5 3698b4 3898b4 3598b4 3398b4 3498b4
  //   3497b4 3497b4 3497b4 3398b4 3197b4 2d96b2 2c96b2 2e96b3 2f96b3 2e95b2 2c95b1 2b95b2 2c95b2 2b94b1
  //   2b94b1 2c94b1 2c95b1 2c94b1 2b94b1 2993b0 2993b0 2793b0 2593b0 2492af 2492af 2292af 2191af 2091ad
  //   2091ad 2090ad 208fad 1f90ad 1c8fad 1a8eac 1a8eac 1a8eac 1b8eac 1b8dac 1a8dab 198cab 168baa 148ba9
  //   138ba9 128aa9 128aa9 1089a7 f89a8 f88a7 e87a6 c87a6 c86a5 d86a5 c86a5 b85a4 b85a4 a84a4 984a3 883a2
  //   783a1 781a1 781a1 680a0 6809f 57f9f 57f9f 57e9d 47d9d 47c9d 47b9c 47b9b 37b9b 37a9b 3799b 2799a
  //   12140f 13150f 141510 161611 171711 171711 171610 191911 191911 1a1911 1b1a11 191911 181811 161710
  //   13160f f130d e130d a0f08 80d06 13160f 151610 11110a 121104 132121 1a3d56 2d3948 38211b 3d1c16 3b1813
  //   3e1510 461511 4c1712 4e1712 4b1811 481a12 451d12 432211 432911 463313 4e4116 574c16 625314 6f5a14
  //   775e15 7c6217 796017 715b14 6c5814 6b5313 825011 8d4310 572d10 2f220d 251507 33210b 4b3814 584416
  //   8f590a c47705 ce900e d5a522 e0b739 e7c24b ebc857 efcb5d efca5e efc95c efc757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
endmodule

module PLU_COLOR_ALU (
  input  [7:0] DATA_A,
  input  EN_A,
  input  EN_OUT,
  input  [7:0] DATA_B,
  input  EN_B,
  input  CLK,
  input  [5:0] opcode,
  output [7:0] DOUT,
  output pixel_clk
);

  wire alu_1_opcode_out;
  wire [7:0] alu_1_dout, demultiplexer_1_out0, demultiplexer_1_out1, multiplexer_1_out, register_1_q,
       register_2_q, register_3_q;

  // Probe on opcode
  Multiplexer #(.width(8)) multiplexer_1 (
    .in0(demultiplexer_1_out0), .in1(DATA_A), .out(multiplexer_1_out), .sel(alu_1_opcode_out));
  // Probe on opcode[4:0]
  // Probe on multiplexer_1_out
  Register register_1 (.D(multiplexer_1_out), .en(EN_A), .clk(CLK), .Q(register_1_q), .clr(1'b0));
  Register register_2 (.D(DATA_B), .en(EN_B), .clk(CLK), .Q(register_2_q), .clr(1'b0));
  // Probe on register_2_q
  // Probe on register_1_q
  // Probe on demultiplexer_1_out0
  ALU alu_1 (
    .A(register_1_q), .B(register_2_q), .opcode(opcode[4:0]), .DOUT(alu_1_dout), .opcode_out(alu_1_opcode_out));
  // Probe on alu_1_dout
  Register register_3 (.D(alu_1_dout), .en(EN_OUT), .clk(CLK), .Q(register_3_q), .clr(1'b0));
  // Probe on register_3_q
  Demultiplexer #(.width(8)) demultiplexer_1 (
    .out0(demultiplexer_1_out0), .out1(demultiplexer_1_out1), .in(register_3_q), .sel(opcode[5]));
  // Probe on demultiplexer_1_out1
  Register register_4 (.D(demultiplexer_1_out1), .en(opcode[5]), .clk(CLK), .Q(DOUT), .clr(1'b0));

  assign pixel_clk = opcode[5];
endmodule

module PLU (
  input  [23:0] DATA_A_IN_24,
  input  [23:0] DATA_B_IN_24,
  input  [2:0] EN_A_3,
  input  [2:0] EN_B_3,
  input  [5:0] Channel_Swap_6,
  input  CLK,
  input  [17:0] opcode_in_18,
  output [23:0] RGB_OUTPUT_24,
  output pixel_clk
);

  wire plu_color_alu_1_pixel_clk, plu_color_alu_2_pixel_clk, plu_color_alu_3_pixel_clk;
  wire [7:0] plu_color_alu_1_dout, plu_color_alu_2_dout, plu_color_alu_3_dout;

  // Probe on opcode_in_18
  // Probe on opcode_in_18[17:12]
  // Probe on opcode_in_18[11:6]
  // Probe on opcode_in_18[5:0]
  PLU_COLOR_ALU plu_color_alu_1 (
    .DATA_A(DATA_A_IN_24[23:16]), .EN_A(EN_A_3[2]), .EN_OUT(1'b1), .DATA_B(DATA_B_IN_24[23:16]),
    .EN_B(EN_B_3[2]), .CLK(CLK), .opcode(opcode_in_18[17:12]), .DOUT(plu_color_alu_1_dout),
    .pixel_clk(plu_color_alu_1_pixel_clk));
  PLU_COLOR_ALU plu_color_alu_2 (
    .DATA_A(DATA_A_IN_24[15:8]), .EN_A(EN_A_3[1]), .EN_OUT(1'b1), .DATA_B(DATA_B_IN_24[15:8]),
    .EN_B(EN_B_3[1]), .CLK(CLK), .opcode(opcode_in_18[11:6]), .DOUT(plu_color_alu_2_dout),
    .pixel_clk(plu_color_alu_2_pixel_clk));
  PLU_COLOR_ALU plu_color_alu_3 (
    .DATA_A(DATA_A_IN_24[7:0]), .EN_A(EN_A_3[0]), .EN_OUT(1'b1), .DATA_B(DATA_B_IN_24[7:0]),
    .EN_B(EN_B_3[0]), .CLK(CLK), .opcode(opcode_in_18[5:0]), .DOUT(plu_color_alu_3_dout),
    .pixel_clk(plu_color_alu_3_pixel_clk));
  // Probe on plu_color_alu_1_dout
  // Probe on plu_color_alu_2_dout
  // Probe on plu_color_alu_3_dout
  COLOR_MUX color_mux_1 (
    .RED_IN(plu_color_alu_1_dout), .GREEN_IN(plu_color_alu_2_dout), .BLUE_IN(plu_color_alu_3_dout),
    .RGB_SELECT(Channel_Swap_6), .RGB_OUT(RGB_OUTPUT_24));
  or or_1 (pixel_clk, plu_color_alu_1_pixel_clk, plu_color_alu_2_pixel_clk, plu_color_alu_3_pixel_clk);
endmodule

module COLOR_MUX (
  input  [7:0] RED_IN,
  input  [7:0] GREEN_IN,
  input  [7:0] BLUE_IN,
  input  [5:0] RGB_SELECT,
  output [23:0] RGB_OUT
);

  Multiplexer #(.select(2), .width(8)) multiplexer_1 (
    .in0(RED_IN), .in1(GREEN_IN), .in2(BLUE_IN), .in3({8{1'b0}}), .out(RGB_OUT[23:16]), .sel(RGB_SELECT[5:4]));
  Multiplexer #(.select(2), .width(8)) multiplexer_2 (
    .in0(RED_IN), .in1(GREEN_IN), .in2(BLUE_IN), .in3({8{1'b0}}), .out(RGB_OUT[15:8]), .sel(RGB_SELECT[3:2]));
  Multiplexer #(.select(2), .width(8)) multiplexer_3 (
    .in0(RED_IN), .in1(GREEN_IN), .in2(BLUE_IN), .in3({8{1'b0}}), .out(RGB_OUT[7:0]), .sel(RGB_SELECT[1:0]));
  // Probe on RGB_SELECT[5:4]
  // Probe on RGB_SELECT[3:2]
  // Probe on RGB_SELECT[1:0]
endmodule

module ALU (
  input  [7:0] A,
  input  [7:0] B,
  input  [4:0] opcode,
  output [7:0] DOUT,
  output opcode_out
);

  wire [7:0] adder_1_out, and_1_out, divider_1_out, multiplier_1_out, nand_1_out, nor_1_out, not_1_out,
       or_1_out, shifter_1_out, subtractor_1_out, xnor_1_out, xor_1_out;

  Adder adder_1 (.a(A), .b(B), .out(adder_1_out));  // open: cin, cout
  Subtractor subtractor_1 (.a(A), .b(B), .out(subtractor_1_out));  // open: bin, bout
  Multiplier multiplier_1 (.a(A), .b(B), .out(multiplier_1_out));  // open: cin, cout
  Divider divider_1 (.a(A), .b(B), .out(divider_1_out));  // open: upper, rem
  Shifter shifter_1 (.in(A), .\dist (B[2:0]), .out(shifter_1_out));
  assign not_1_out = ~A;  // NOT_Gate not_1, 8 bits wide
  assign and_1_out = A & B;  // AND_Gate and_1, 8 bits wide
  assign or_1_out = A | B;  // OR_Gate or_1, 8 bits wide
  assign nand_1_out = ~(A & B);  // NAND_Gate nand_1, 8 bits wide
  assign nor_1_out = ~(A | B);  // NOR_Gate nor_1, 8 bits wide
  assign xor_1_out = A ^ B;  // XOR_Gate xor_1, 8 bits wide
  assign xnor_1_out = ~(A ^ B);  // XNOR_Gate xnor_1, 8 bits wide
  Multiplexer #(.select(4), .width(8)) multiplexer_1 (
    .in0(A), .in1(B), .in2(adder_1_out), .in3(subtractor_1_out), .in4(multiplier_1_out), .in5(divider_1_out),
    .in6(shifter_1_out), .in7(not_1_out), .in8(and_1_out), .in9(or_1_out), .in10(nand_1_out),
    .in11(nor_1_out), .in12(xor_1_out), .in13(xnor_1_out), .in14({8{1'b0}}), .in15({8{1'b1}}), .out(DOUT),
    .sel(opcode[3:0]));

  assign opcode_out = opcode[4];
endmodule
